// Logisim project 2sComplementCircuit.circ as structural Verilog: 1 circuit, main circuit main
module main (
  input  in_1,
  input  A,
  input  A_2,
  input  B,
  input  B_2,
  input  A_3,
  input  A_4,
  input  B_3,
  input  B_4,
  output Output,
  output Output_2,
  output Output_3,
  output Output_4,
  output Carry_Out
);

  wire and_1_out, and_2_out, and_3_out, and_4_out, and_5_out, and_6_out, and_7_out, and_8_out, and_9_out,
       and_10_out, and_11_out, and_12_out, and_13_out, and_14_out, and_15_out, and_16_out, and_17_out,
       and_18_out, and_19_out, and_20_out, and_21_out, and_22_out, and_23_out, and_24_out, and_25_out,
       and_26_out, and_27_out, and_28_out, nor_3_out, nor_5_out, or_1_out;

  and and_1 (and_1_out, ~in_1, ~A, B);  // AND_Gate
  and and_2 (and_2_out, ~in_1, A, ~B);  // AND_Gate
  and and_3 (and_3_out, in_1, ~A, B);  // AND_Gate
  and and_4 (and_4_out, in_1, A, ~B);  // AND_Gate
  and and_5 (and_5_out, ~in_1, A, B);  // AND_Gate
  and and_6 (and_6_out, in_1, A, B);
  and and_7 (and_7_out, in_1, ~A, ~B);  // AND_Gate
  and and_8 (and_8_out, ~or_1_out, ~A_4, B_4);  // AND_Gate
  and and_9 (and_9_out, ~or_1_out, A_4, ~B_4);  // AND_Gate
  and and_10 (and_10_out, or_1_out, ~A_4, B_4);  // AND_Gate
  and and_11 (and_11_out, or_1_out, A_4, ~B_4);  // AND_Gate
  and and_12 (and_12_out, ~or_1_out, A_4, B_4);  // AND_Gate
  and and_13 (and_13_out, or_1_out, A_4, B_4);
  and and_14 (and_14_out, or_1_out, ~A_4, ~B_4);  // AND_Gate
  nor nor_1 (Output, and_1_out, and_2_out, and_7_out, and_6_out);
  or or_1 (or_1_out, and_5_out, and_3_out, and_6_out, and_4_out);
  nor nor_2 (Output_4, and_8_out, and_9_out, and_14_out, and_13_out);
  nor nor_3 (nor_3_out, and_12_out, and_10_out, and_13_out, and_11_out);
  and and_15 (and_15_out, ~nor_3_out, A_2, ~B_2);  // AND_Gate
  and and_16 (and_16_out, nor_3_out, ~A_2, B_2);  // AND_Gate
  and and_17 (and_17_out, ~nor_3_out, ~A_2, B_2);  // AND_Gate
  and and_18 (and_18_out, ~nor_3_out, A_2, B_2);  // AND_Gate
  and and_19 (and_19_out, nor_3_out, A_2, B_2);
  and and_20 (and_20_out, nor_3_out, ~A_2, ~B_2);  // AND_Gate
  and and_21 (and_21_out, nor_3_out, A_2, ~B_2);  // AND_Gate
  nor nor_4 (Output_2, and_17_out, and_15_out, and_20_out, and_19_out);
  nor nor_5 (nor_5_out, and_18_out, and_16_out, and_19_out, and_21_out);
  and and_22 (and_22_out, ~nor_5_out, ~A_3, B_3);  // AND_Gate
  and and_23 (and_23_out, ~nor_5_out, A_3, B_3);  // AND_Gate
  and and_24 (and_24_out, ~nor_5_out, A_3, ~B_3);  // AND_Gate
  and and_25 (and_25_out, nor_5_out, A_3, B_3);
  and and_26 (and_26_out, nor_5_out, ~A_3, B_3);  // AND_Gate
  and and_27 (and_27_out, nor_5_out, ~A_3, ~B_3);  // AND_Gate
  and and_28 (and_28_out, nor_5_out, A_3, ~B_3);  // AND_Gate
  Adder #(.width(1)) adder_1 ();  // open: a, b, out, cin, cout
  nor nor_6 (Output_3, and_22_out, and_24_out, and_27_out, and_25_out);
  nor nor_7 (Carry_Out, and_23_out, and_26_out, and_25_out, and_28_out);
endmodule
