// Logisim project 3BitAdder.circ as structural Verilog: 1 circuit, main circuit main
module main (
  input  in_1,
  input  in_2,
  input  in_3,
  input  in_4,
  input  in_5,
  input  in_6,
  input  in_7,
  output out_8,
  output out_9,
  output out_10,
  output out_11
);

  wire and_1_out, and_2_out, and_3_out, and_4_out, and_5_out, and_6_out, or_2_out, or_3_out, xor_2_out,
       xor_4_out, xor_5_out;

  and and_1 (and_1_out, xor_2_out, or_2_out);
  or or_1 (out_11, and_2_out, and_1_out);
  and and_2 (and_2_out, in_4, in_1);
  xor xor_1 (out_8, or_2_out, xor_2_out);
  xor xor_2 (xor_2_out, in_1, in_4);
  and and_3 (and_3_out, xor_4_out, or_3_out);
  or or_2 (or_2_out, and_4_out, and_3_out);
  and and_4 (and_4_out, in_5, in_2);
  xor xor_3 (out_9, or_3_out, xor_4_out);
  xor xor_4 (xor_4_out, in_2, in_5);
  or or_3 (or_3_out, and_5_out, and_6_out);
  and and_5 (and_5_out, in_6, in_3);
  and and_6 (and_6_out, xor_5_out, in_7);
  xor xor_5 (xor_5_out, in_3, in_6);
  xor xor_6 (out_10, in_7, xor_5_out);

  // Notes on the sheet:
  //   101
  //   001
  //           0110
  //   110
  //   101
  //        1011
  //   111
  //   111
  //         1110
endmodule
