// Logisim project FullAdder.circ as structural Verilog: 1 circuit, main circuit main
module main (
  input  in_1,
  input  A,
  input  A_2,
  input  B,
  input  B_2,
  input  A_3,
  input  A_4,
  input  B_3,
  input  B_4,
  output Output,
  output Output_2,
  output Output_3,
  output Output_4,
  output Carry_Out
);

  wire and_1_out, and_2_out, and_3_out, and_4_out, and_5_out, and_6_out, and_7_out, and_8_out, and_9_out,
       and_10_out, and_11_out, and_12_out, and_13_out, and_14_out, and_15_out, and_16_out, and_17_out,
       and_18_out, and_19_out, and_20_out, and_21_out, and_22_out, and_23_out, and_24_out, and_25_out,
       and_26_out, and_27_out, and_28_out, or_2_out, or_4_out, or_6_out;

  and and_1 (and_1_out, ~in_1, ~A, B);  // AND_Gate
  and and_2 (and_2_out, ~in_1, A, ~B);  // AND_Gate
  and and_3 (and_3_out, in_1, ~A, B);  // AND_Gate
  and and_4 (and_4_out, in_1, A, ~B);  // AND_Gate
  and and_5 (and_5_out, ~in_1, A, B);  // AND_Gate
  and and_6 (and_6_out, in_1, A, B);
  and and_7 (and_7_out, in_1, ~A, ~B);  // AND_Gate
  and and_8 (and_8_out, ~or_2_out, ~A_4, B_4);  // AND_Gate
  and and_9 (and_9_out, ~or_2_out, A_4, ~B_4);  // AND_Gate
  and and_10 (and_10_out, or_2_out, ~A_4, B_4);  // AND_Gate
  and and_11 (and_11_out, or_2_out, A_4, ~B_4);  // AND_Gate
  and and_12 (and_12_out, ~or_2_out, A_4, B_4);  // AND_Gate
  and and_13 (and_13_out, or_2_out, A_4, B_4);
  and and_14 (and_14_out, or_2_out, ~A_4, ~B_4);  // AND_Gate
  or or_1 (Output, and_1_out, and_2_out, and_7_out, and_6_out);
  or or_2 (or_2_out, and_5_out, and_3_out, and_6_out, and_4_out);
  or or_3 (Output_4, and_8_out, and_9_out, and_14_out, and_13_out);
  or or_4 (or_4_out, and_12_out, and_10_out, and_13_out, and_11_out);
  and and_15 (and_15_out, ~or_4_out, A_2, ~B_2);  // AND_Gate
  and and_16 (and_16_out, or_4_out, ~A_2, B_2);  // AND_Gate
  and and_17 (and_17_out, ~or_4_out, ~A_2, B_2);  // AND_Gate
  and and_18 (and_18_out, ~or_4_out, A_2, B_2);  // AND_Gate
  and and_19 (and_19_out, or_4_out, A_2, B_2);
  and and_20 (and_20_out, or_4_out, ~A_2, ~B_2);  // AND_Gate
  and and_21 (and_21_out, or_4_out, A_2, ~B_2);  // AND_Gate
  or or_5 (Output_2, and_17_out, and_15_out, and_20_out, and_19_out);
  or or_6 (or_6_out, and_18_out, and_16_out, and_19_out, and_21_out);
  and and_22 (and_22_out, ~or_6_out, ~A_3, B_3);  // AND_Gate
  and and_23 (and_23_out, ~or_6_out, A_3, B_3);  // AND_Gate
  and and_24 (and_24_out, ~or_6_out, A_3, ~B_3);  // AND_Gate
  and and_25 (and_25_out, or_6_out, A_3, B_3);
  and and_26 (and_26_out, or_6_out, ~A_3, B_3);  // AND_Gate
  and and_27 (and_27_out, or_6_out, ~A_3, ~B_3);  // AND_Gate
  and and_28 (and_28_out, or_6_out, A_3, ~B_3);  // AND_Gate
  Adder #(.width(1)) adder_1 ();  // open: a, b, out, cin, cout
  or or_7 (Output_3, and_22_out, and_24_out, and_27_out, and_25_out);
  or or_8 (Carry_Out, and_23_out, and_26_out, and_25_out, and_28_out);
endmodule
