// Logisim project NOR and NAND.circ as structural Verilog: 1 circuit, main circuit main
module main (
  input  A,
  input  B,
  input  in_3,
  input  in_4,
  output out_5,
  output out_6
);

  wire transistor_5_out, transistor_6_out;

  Transistor #(.\type ("n")) transistor_1 (.in(1'b0), .out(out_6), .gate(in_3));
  Transistor transistor_2 (.in(1'b1), .out(out_5), .gate(B));
  Transistor transistor_3 (.in(1'b1), .out(out_5), .gate(A));
  Transistor #(.\type ("n")) transistor_4 (.in(transistor_5_out), .out(out_5), .gate(A));
  Transistor #(.\type ("n")) transistor_5 (.in(1'b0), .out(transistor_5_out), .gate(B));
  Transistor transistor_6 (.in(1'b1), .out(transistor_6_out), .gate(in_3));
  Transistor transistor_7 (.in(transistor_6_out), .out(out_6), .gate(in_4));
  Transistor #(.\type ("n")) transistor_8 (.in(1'b0), .out(out_6), .gate(in_4));

  // Notes on the sheet:
  //   NAND Gate
  //   NOR Gate
endmodule
